// Logisim project Circuit.circ as structural Verilog: 3 circuits, main circuit main
module main (
  output out_1
);

  wire Clear_SC, Clock, d_ff_1_q, INC_AC, INC_AR, INC_DR, INC_PC, Load_AC, Load_AR, Load_DR, Load_IR,
       Load_PC, Load_TR, not_1_out, Read, Selection_Bus_AC, Selection_Bus_AR, Selection_Bus_DR,
       Selection_Bus_IR, Selection_Bus_PC, Selection_Bus_TR, Write;
  wire [2:0] priority_encoder_1_out, Selection_line_ALU;
  wire [3:0] SC;
  wire [6:0] AR_q, bit_extender_1_out;
  wire [15:0] AC, alu_1_ac_output, bit_extender_2_out, DR, IR, multiplexer_1_out, PC_q, ram_1_data, TR_q;

  Clock clock_1 (.out(Clock));
  not not_1 (not_1_out, Clear_SC);
  Bit_Extender #(.in_width(16), .out_width(7)) bit_extender_1 (.in(multiplexer_1_out), .out(bit_extender_1_out));
  Counter #(.width(4), .max('hf)) u_SC (
    .count(not_1_out), .Q(SC), .clk(Clock), .clr(d_ff_1_q));  // open: load, D, carry
  D_Flip_Flop d_ff_1 (.clk(Clock), .D(Clear_SC), .Q(d_ff_1_q), .en(1'b1));  // open: Qn, preset, reset
  Counter #(.width(16), .max('hffff)) PC (
    .load(Load_PC), .D(multiplexer_1_out), .count(INC_PC), .Q(PC_q), .clk(Clock));  // open: carry, clr
  Register #(.width(7)) AR (.D(bit_extender_1_out), .en(Load_AR), .Q(AR_q), .clk(Clock));  // open: clr
  Register #(.width(16)) TR (.D(multiplexer_1_out), .en(Load_TR), .Q(TR_q), .clk(Clock));  // open: clr
  Register #(.width(16)) u_DR (.D(multiplexer_1_out), .en(Load_DR), .Q(DR), .clk(Clock));  // open: clr
  Register #(.width(16)) u_AC (.D(alu_1_ac_output), .en(Load_AC), .Q(AC), .clk(Clock));  // open: clr
  Register #(.width(16)) u_IR (.D(multiplexer_1_out), .en(Load_IR), .Q(IR), .clk(Clock));  // open: clr
  RAM #(.addrWidth(7), .dataWidth(16), .bus("separate")) ram_1 (
    .addr(AR_q), .din(multiplexer_1_out), .data(ram_1_data), .str(Write), .clk(Clock), .ld(Read));  // open: sel, clr
  Control_Unit control_unit_1 (
    .IR(IR), .SC(SC), .AC(AC), .DR(DR), .Read(Read), .Load_AR(Load_AR), .Write(Write), .Load_PC(Load_PC),
    .Load_TR(Load_TR), .Load_DR(Load_DR), .Selection_Bus_PC(Selection_Bus_PC), .Load_IR(Load_IR),
    .Selection_Bus_AR(Selection_Bus_AR), .Load_AC(Load_AC), .Selection_Bus_DR(Selection_Bus_DR),
    .Selection_Bus_TR(Selection_Bus_TR), .Selection_Bus_IR(Selection_Bus_IR),
    .Selection_Bus_AC(Selection_Bus_AC), .INC_AR(INC_AR), .INC_PC(INC_PC), .Clear_SC(Clear_SC),
    .INC_DR(INC_DR), .INC_AC(INC_AC), .Selection_line_ALU(Selection_line_ALU));
  assign bit_extender_2_out = {{9{1'b0}}, AR_q};  // Bit_Extender bit_extender_2
  ALU alu_1 (.A(DR), .B(AC), .in_3(Selection_line_ALU), .E(out_1), .AC_Output(alu_1_ac_output));
  Multiplexer #(.select(3), .width(16)) multiplexer_1 (
    .in0(ram_1_data), .in1(bit_extender_2_out), .in2(TR_q), .in3(DR), .in4(AC), .in5(PC_q), .in6(IR),
    .out(multiplexer_1_out), .sel(priority_encoder_1_out), .en(1'b1));  // open: in7
  Priority_Encoder priority_encoder_1 (
    .in0(Read), .in1(Selection_Bus_AR), .in2(Selection_Bus_TR), .in3(Selection_Bus_DR),
    .in4(Selection_Bus_AC), .in5(Selection_Bus_PC), .in6(Selection_Bus_IR), .out(priority_encoder_1_out),
    .en_in(1'b1));  // open: in7, gs, en_out
endmodule

module ALU (
  input  [15:0] A,
  input  [15:0] B,
  input  [2:0] in_3,
  output E,
  output [15:0] AC_Output
);

  wire adder_1_cout, adder_2_cout, subtractor_1_bout;
  wire [15:0] adder_1_out, adder_2_out, and_1_out, or_1_out, subtractor_1_out, xor_1_out;

  Adder #(.width(16)) adder_1 (.a(A), .b(B), .out(adder_1_out), .cin(1'b0), .cout(adder_1_cout));
  Subtractor #(.width(16)) subtractor_1 (.a(A), .b(B), .out(subtractor_1_out), .bin(1'b0), .bout(subtractor_1_bout));
  assign and_1_out = A & B;  // AND_Gate and_1, 16 bits wide
  assign or_1_out = A | B;  // OR_Gate or_1, 16 bits wide
  assign xor_1_out = A ^ B;  // XOR_Gate xor_1, 16 bits wide
  Adder #(.width(16)) adder_2 (.a(A), .b({16{1'b0}}), .out(adder_2_out), .cin(1'b1), .cout(adder_2_cout));
  or or_2 (E, adder_1_cout, subtractor_1_bout, adder_2_cout);
  Multiplexer #(.select(3), .width(16)) multiplexer_1 (
    .in1(adder_1_out), .in2(subtractor_1_out), .in3(A), .in4(and_1_out), .in5(or_1_out), .in6(xor_1_out),
    .in7(adder_2_out), .out(AC_Output), .sel(in_3));  // open: in0, en
endmodule

module Control_Unit (
  input  [15:0] IR,
  input  [3:0] SC,
  input  [15:0] AC,
  input  [15:0] DR,
  output Read,
  output Load_AR,
  output Write,
  output Load_PC,
  output Load_TR,
  output Load_DR,
  output Selection_Bus_PC,
  output Load_IR,
  output Selection_Bus_AR,
  output Load_AC,
  output Selection_Bus_DR,
  output Selection_Bus_TR,
  output Selection_Bus_IR,
  output Selection_Bus_AC,
  output INC_AR,
  output INC_PC,
  output Clear_SC,
  output INC_DR,
  output INC_AC,
  output [2:0] Selection_line_ALU
);

  wire AC_IS_ZERO, D0, D0T4, D0T5, D1, D1T4, D1T5, D2, D2T4, D2T5, D3, D3T4, D4, D4T4, D5, D5T4, D5T5, D5T6,
       D5T7, D6, D6T4, D6T5, D6T6, D6T6DRZERO, D7, DR_IS_ZERO, I_prime_D7T3B2, I_prime_D7T3B5,
       I_prime_D7T4B5, not_3_out, not_4_out, not_5_out, or_1_out, or_2_out, r, rB2, rB2ACZERO, rB5, T0, T2,
       T3, T4, T5, T6, T7, T8, T9, T10, T11, T12, T13, T14, T15, Transfer;

  or or_1 (or_1_out, AC[0], AC[1], AC[2], AC[3], AC[4], AC[5], AC[6], AC[7], AC[8], AC[9], AC[10], AC[11], AC[12], AC[13], AC[14], AC[15]);
  Decoder #(.select(4)) decoder_1 (
    .out0(T0), .out1(Load_IR), .out2(T2), .out3(T3), .out4(T4), .out5(T5), .out6(T6), .out7(T7), .out8(T8),
    .out9(T9), .out10(T10), .out11(T11), .out12(T12), .out13(T13), .out14(T14), .out15(T15), .sel(SC),
    .en(1'b1));
  not not_1 (AC_IS_ZERO, or_1_out);
  not not_2 (DR_IS_ZERO, or_2_out);
  or or_2 (or_2_out, DR[0], DR[1], DR[2], DR[3], DR[4], DR[5], DR[6], DR[7], DR[8], DR[9], DR[10], DR[11], DR[12], DR[13], DR[14], DR[15]);
  Decoder #(.select(3)) decoder_2 (
    .out0(D0), .out1(D1), .out2(D2), .out3(D3), .out4(D4), .out5(D5), .out6(D6), .out7(D7), .sel(IR[14:12]),
    .en(1'b1));
  and and_1 (r, D7, T3);
  and and_2 (D6T6, D6, T6);
  and and_3 (rB2, r, IR[2]);
  and and_4 (rB5, r, IR[5]);
  and and_5 (D0T5, D0, T5);
  and and_6 (D4T4, D4, T4);
  and and_7 (D5T5, D5, T5);
  and and_8 (D0T4, D0, T4);
  and and_9 (D1T4, D1, T4);
  and and_10 (D2T4, D2, T4);
  and and_11 (D6T4, D6, T4);
  not not_3 (not_3_out, IR[15]);
  not not_4 (not_4_out, IR[15]);
  and and_12 (D2T5, D2, T5);
  and and_13 (D5T7, D5, T7);
  and and_14 (I_prime_D7T3B5, not_3_out, D7, T3, IR[5]);
  and and_15 (I_prime_D7T3B2, not_4_out, D7, T3, IR[2]);
  and and_16 (D0T5, D0, T5);
  and and_17 (D1T5, D1, T5);
  and and_18 (D2T5, D2, T5);
  and and_19 (D5T6, D5, T6);
  or or_3 (Transfer, D5T5, D2T5);
  not not_5 (not_5_out, IR[15]);
  or or_4 (Load_AR, T0, T2);
  buf or_5 (Load_PC, D4T4);  // OR_Gate
  buf or_6 (Selection_Bus_TR, D5T6);  // OR_Gate
  and and_20 (I_prime_D7T4B5, not_5_out, D7, T4, IR[5]);
  or or_7 (Load_DR, I_prime_D7T3B5, D0T4, D5T4, D2T4, D5T6, D1T4);
  or or_8 (Load_AC, D1T5, D5T7, D2T5, D0T5, D5T5, I_prime_D7T4B5);
  and and_21 (D3T4, D3, T4);
  and and_22 (D5T5, D5, T5);
  and and_23 (D5T4, D5, T4);
  or or_9 (Clear_SC, I_prime_D7T4B5, I_prime_D7T3B2, D0T5, D1T5, D3T4, D4T4, D5T7, D2T5);
  and and_24 (D6T5, D6, T5);
  and and_25 (rB2ACZERO, I_prime_D7T3B2, AC_IS_ZERO);
  Priority_Encoder priority_encoder_1 (
    .in1(D1T5), .in2(D5T7), .in3(Transfer), .in4(D0T5), .in7(I_prime_D7T4B5), .out(Selection_line_ALU),
    .en_in(1'b1));  // open: in0, in5, in6, gs, en_out
  or or_10 (Read, Load_IR, D2T4, D0T4, D1T4, D5T4);
  buf or_11 (Write, D3T4);  // OR_Gate
  buf or_12 (Load_TR, D5T5);  // OR_Gate
  buf or_13 (Selection_Bus_PC, T0);  // OR_Gate
  buf or_14 (Selection_Bus_AR, D4T4);  // OR_Gate
  or or_15 (Selection_Bus_DR, D5T5, D2T5);
  buf or_16 (Selection_Bus_IR, T2);  // OR_Gate
  or or_17 (Selection_Bus_AC, I_prime_D7T3B5, D3T4, D5T5);
  and and_26 (D6T6DRZERO, D6T6, DR_IS_ZERO);
  buf or_18 (INC_AR, D5T4);  // OR_Gate
  or or_19 (INC_PC, Load_IR, rB2ACZERO);
  buf or_20 (INC_AC, rB5);  // OR_Gate

  // Other names for the same wires on the sheet: B0 = IR[0]; B1 = IR[1]; B2 = IR[2]; B3 = IR[3]; B4 = IR[4];
  //   B5 = IR[5]; B6 = IR[6]; B7 = IR[7]; B8 = IR[8]; B9 = IR[9]; B10 = IR[10]; B11 = IR[11]; Ibit = IR[15];
  //   T1 = Load_IR
endmodule
